# Fritzing sketch sketch (saved by Fritzing 0.9.3b)
breadboards: 2

parts:
  U1 = LuaNode32 / ESP32
  S1 = Momentary Switch [package=ksa_sealed_tac_switch]
  S2 = Momentary Switch [package=ksa_sealed_tac_switch]
  S3 = Momentary Switch [package=ksa_sealed_tac_switch]
  S4 = Momentary Switch [package=ksa_sealed_tac_switch]
  S5 = Momentary Switch [package=ksa_sealed_tac_switch]
  S6 = Momentary Switch [package=ksa_sealed_tac_switch]
  S7 = Momentary Switch [package=ksa_sealed_tac_switch]
  S8 = Momentary Switch [package=ksa_sealed_tac_switch]
  S9 = Momentary Switch [package=ksa_sealed_tac_switch]
  R3 = Resistor [tolerance=±5% resistance=220 package="0805 [SMD]"]
  R4 = Resistor [tolerance=±5% resistance=220 package="0805 [SMD]"]
  R5 = Resistor [tolerance=±5% resistance=220 package="0805 [SMD]"]
  R6 = Resistor [tolerance=±5% resistance=220 package="0805 [SMD]"]
  R7 = Resistor [tolerance=±5% resistance=220 package="0805 [SMD]"]
  R8 = Resistor [tolerance=±5% resistance=220 package="0805 [SMD]"]
  R9 = Resistor [tolerance=±5% resistance=220 package="0805 [SMD]"]
  R10 = Resistor [tolerance=±5% resistance=220 package="0805 [SMD]"]
  R11 = Resistor [tolerance=±5% resistance=220 package="0805 [SMD]"]
  LED1 = smd LED [color="Red (633nm)" package="0805 [SMD]"]
  LED4 = smd LED [color="Red (633nm)" package="0805 [SMD]"]
  LED5 = smd LED [color="Red (633nm)" package="0805 [SMD]"]
  LED6 = smd LED [color="Red (633nm)" package="0805 [SMD]"]
  LED7 = smd LED [color="Red (633nm)" package="0805 [SMD]"]
  LED8 = smd LED [color="Red (633nm)" package="0805 [SMD]"]
  LED9 = RGB LED (com. cathode, rbg) [package="5 mm [THT]"]
  Squix1 = OLED 0.96" 128x64 I2C SSD1306

nets:
  N1: U1.EN, S1.4
  N2: U1.VP, S2.4
  N3: U1.VN, S3.4
  N4: U1.D34, S4.4
  N5: U1.D35, S5.4
  N6: U1.D32, S6.4
  N7: U1.D33, S7.4
  N8: U1.D25, S8.4
  N9: U1.D26, S9.4
  N10: U1.D27, LED9.green_anode
  N11: U1.D14, LED9.common_cathode
  N12: U1.D12, LED9.red_anode
  GND: U1.GND, R3.Pin_0, R4.Pin_0, R5.Pin_0, R6.Pin_0, R7.Pin_0, R8.Pin_0, R9.Pin_0, R10.Pin_0, R11.Pin_0, LED1.anode, LED4.anode, LED5.anode, LED6.anode, LED7.anode, LED8.anode, LED9.blue_anode, Squix1.GND
  3V3: U1.3V3, S1.1, S2.1, S3.1, S4.1, S5.1, S6.1, S7.1, S8.1, S9.1, Squix1.VCC
  N13: U1.RX2, LED8.cathode
  N14: U1.TX2, LED7.cathode
  N15: U1.D5, LED6.cathode
  N16: U1.D18, LED5.cathode
  N17: U1.D19, LED4.cathode
  N18: U1.D21, Squix1.SCA
  N19: U1.D22, Squix1.SCL
  N20: U1.D23, LED1.cathode
  N21: S1.3, R3.Pin_1
  N22: S2.3, R4.Pin_1
  N23: S3.3, R5.Pin_1
  N24: S4.3, R6.Pin_1
  N25: S5.3, R7.Pin_1
  N26: S6.3, R8.Pin_1
  N27: S7.3, R9.Pin_1
  N28: S8.3, R10.Pin_1
  N29: S9.3, R11.Pin_1

custom parts:
  LuaNode32 / ESP32: ESP32 based LuaNode32
